# Fritzing sketch pixel (saved by Fritzing 0.9.1b)
circuit board: 5.25727cm x 3.53527cm
breadboards: 1

parts:
  J1 = double row rounded female pin header, 6 pins [form="♀ (female rounded)"]
  IR1 = TSOP312.., 314.. [package=THT]
  IR = LED - 5mm [color="Infrared (940nm)" package="5 mm [THT]"]
  R1 = Resistor [tolerance=±5% resistance=220 package=THT]
  R2 = Resistor [tolerance=±5% resistance=220 package=THT]
  RED = LED - 3mm [color="Red (633nm)" package="3 mm [THT]"]

nets:
  N1: J1.pin1, IR1.GND, IR.cathode, RED.cathode
  N2: J1.pin2, IR1.Vs
  N3: J1.pin3, IR1.Data
  N4: J1.pin4, R1.Pin_1
  N5: J1.pin5, R2.Pin_1
  N6: IR.anode, R2.Pin_0
  N7: R1.Pin_0, RED.anode
